// Logisim project CPU.circ as structural Verilog: 4 circuits, main circuit implementation
module implementation (
  input  [15:0] Instruction_In,
  input  ClkIn,
  output [4:0] Instruction_Address_Out,
  output [3:0] Reg0_Out,
  output [3:0] Reg1_Out,
  output [3:0] Reg2_Out,
  output [3:0] Reg3_Out,
  output [3:0] Reg4_Out,
  output [3:0] Reg5_Out,
  output [3:0] Reg6_Out,
  output [3:0] Reg7_Out,
  output [3:0] Reg8_Out,
  output [3:0] Reg9_Out,
  output [3:0] Reg10_Out,
  output [3:0] Reg11_Out,
  output [3:0] Reg12_Out,
  output [3:0] Reg13_Out,
  output [3:0] Reg14_Out,
  output [3:0] Reg15_Out
);

  wire isImmediate, isStop, not_1_out, RegWrite;
  wire [3:0] A_Value, alu_1_aluresult, B_Value, multiplexer_1_out;
  wire [4:0] adder_1_out;

  not not_1 (not_1_out, isStop);
  Register #(.width(5)) register_1 (
    .D(adder_1_out), .en(not_1_out), .clk(ClkIn), .Q(Instruction_Address_Out));  // open: clr
  Adder #(.width(5)) adder_1 (.a(5'b00001), .b(Instruction_Address_Out), .out(adder_1_out));  // open: cin, cout
  Multiplexer #(.enable("false"), .width(4)) multiplexer_1 (
    .in0(B_Value), .in1(Instruction_In[3:0]), .out(multiplexer_1_out), .sel(isImmediate));
  ALU alu_1 (.ALU_OPin(Instruction_In[15:12]), .Ain(A_Value), .Bin(multiplexer_1_out), .ALUresult(alu_1_aluresult));
  InstructionDecoder instructiondecoder_1 (
    .OpCodeIn(Instruction_In[15:12]), .RegWrite(RegWrite), .isImmediate(isImmediate), .isStop(isStop));
  RegFile regfile_1 (
    .A_Sel_In(Instruction_In[7:4]), .B_Sel_In(Instruction_In[3:0]), .C_Sel_In(Instruction_In[11:8]),
    .Data_In(alu_1_aluresult), .Reg_Write_In(RegWrite), .clk_in(ClkIn), .A_Out(A_Value), .B_Out(B_Value),
    .Reg0_Out(Reg0_Out), .Reg1_Out(Reg1_Out), .Reg2_Out(Reg2_Out), .Reg3_Out(Reg3_Out), .Reg4_Out(Reg4_Out),
    .Reg5_Out(Reg5_Out), .Reg6_Out(Reg6_Out), .Reg7_Out(Reg7_Out), .Reg8_Out(Reg8_Out), .Reg9_Out(Reg9_Out),
    .Reg10_Out(Reg10_Out), .Reg11_Out(Reg11_Out), .Reg12_Out(Reg12_Out), .Reg13_Out(Reg13_Out),
    .Reg14_Out(Reg14_Out), .Reg15_Out(Reg15_Out));

  // Other names for the same wires on the sheet: Clk = ClkIn; B[3:0] = Instruction_In[3:0];
  //   Immediate[3:0] = Instruction_In[3:0]; Instruction[15:0] = Instruction_In; A[3:0] = Instruction_In[7:4];
  //   C[3:0] = Instruction_In[11:8]; OpCode[3:0] = Instruction_In[15:12];
  //   Instruction_Address[4:0] = Instruction_Address_Out; Reg0[3:0] = Reg0_Out; Reg1[3:0] = Reg1_Out;
  //   Reg2[3:0] = Reg2_Out; Reg3[3:0] = Reg3_Out; Reg4[3:0] = Reg4_Out; Reg5[3:0] = Reg5_Out; Reg6[3:0] = Reg6_Out;
  //   Reg7[3:0] = Reg7_Out; Reg8[3:0] = Reg8_Out; Reg9[3:0] = Reg9_Out; Reg10[3:0] = Reg10_Out;
  //   Reg11[3:0] = Reg11_Out; Reg12[3:0] = Reg12_Out; Reg13[3:0] = Reg13_Out; Reg14[3:0] = Reg14_Out;
  //   Reg15[3:0] = Reg15_Out

  // Notes on the sheet:
  //   Kabir Athwal & Suba Kanchadapu 
endmodule

module RegFile (
  input  [3:0] A_Sel_In,
  input  [3:0] B_Sel_In,
  input  [3:0] C_Sel_In,
  input  [3:0] Data_In,
  input  Reg_Write_In,
  input  clk_in,
  output [3:0] A_Out,
  output [3:0] B_Out,
  output [3:0] Reg0_Out,
  output [3:0] Reg1_Out,
  output [3:0] Reg2_Out,
  output [3:0] Reg3_Out,
  output [3:0] Reg4_Out,
  output [3:0] Reg5_Out,
  output [3:0] Reg6_Out,
  output [3:0] Reg7_Out,
  output [3:0] Reg8_Out,
  output [3:0] Reg9_Out,
  output [3:0] Reg10_Out,
  output [3:0] Reg11_Out,
  output [3:0] Reg12_Out,
  output [3:0] Reg13_Out,
  output [3:0] Reg14_Out,
  output [3:0] Reg15_Out
);

  wire Reg_Write0, Reg_Write1, Reg_Write2, Reg_Write3, Reg_Write4, Reg_Write5, Reg_Write6, Reg_Write7,
       Reg_Write8, Reg_Write9, Reg_Write10, Reg_Write11, Reg_Write12, Reg_Write13, Reg_Write14, Reg_Write15;

  Demultiplexer #(.enable("false"), .select(4)) demultiplexer_1 (
    .out0(Reg_Write0), .out1(Reg_Write1), .out2(Reg_Write2), .out3(Reg_Write3), .out4(Reg_Write4),
    .out5(Reg_Write5), .out6(Reg_Write6), .out7(Reg_Write7), .out8(Reg_Write8), .out9(Reg_Write9),
    .out10(Reg_Write10), .out11(Reg_Write11), .out12(Reg_Write12), .out13(Reg_Write13), .out14(Reg_Write14),
    .out15(Reg_Write15), .in(Reg_Write_In), .sel(C_Sel_In));
  Register #(.width(4)) register_1 (.D(Data_In), .en(Reg_Write0), .clk(clk_in), .Q(Reg0_Out));  // open: clr
  Register #(.width(4)) register_2 (.D(Data_In), .en(Reg_Write4), .clk(clk_in), .Q(Reg4_Out));  // open: clr
  Register #(.width(4)) register_3 (.D(Data_In), .en(Reg_Write8), .clk(clk_in), .Q(Reg8_Out));  // open: clr
  Register #(.width(4)) register_4 (.D(Data_In), .en(Reg_Write12), .clk(clk_in), .Q(Reg12_Out));  // open: clr
  Register #(.width(4)) register_5 (.D(Data_In), .en(Reg_Write1), .clk(clk_in), .Q(Reg1_Out));  // open: clr
  Register #(.width(4)) register_6 (.D(Data_In), .en(Reg_Write5), .clk(clk_in), .Q(Reg5_Out));  // open: clr
  Register #(.width(4)) register_7 (.D(Data_In), .en(Reg_Write9), .clk(clk_in), .Q(Reg9_Out));  // open: clr
  Register #(.width(4)) register_8 (.D(Data_In), .en(Reg_Write13), .clk(clk_in), .Q(Reg13_Out));  // open: clr
  Register #(.width(4)) register_9 (.D(Data_In), .en(Reg_Write2), .clk(clk_in), .Q(Reg2_Out));  // open: clr
  Register #(.width(4)) register_10 (.D(Data_In), .en(Reg_Write6), .clk(clk_in), .Q(Reg6_Out));  // open: clr
  Register #(.width(4)) register_11 (.D(Data_In), .en(Reg_Write10), .clk(clk_in), .Q(Reg10_Out));  // open: clr
  Register #(.width(4)) register_12 (.D(Data_In), .en(Reg_Write14), .clk(clk_in), .Q(Reg14_Out));  // open: clr
  Register #(.width(4)) register_13 (.D(Data_In), .en(Reg_Write3), .clk(clk_in), .Q(Reg3_Out));  // open: clr
  Register #(.width(4)) register_14 (.D(Data_In), .en(Reg_Write7), .clk(clk_in), .Q(Reg7_Out));  // open: clr
  Register #(.width(4)) register_15 (.D(Data_In), .en(Reg_Write11), .clk(clk_in), .Q(Reg11_Out));  // open: clr
  Register #(.width(4)) register_16 (.D(Data_In), .en(Reg_Write15), .clk(clk_in), .Q(Reg15_Out));  // open: clr
  Multiplexer #(.enable("false"), .select(4), .width(4)) multiplexer_1 (
    .in0(Reg0_Out), .in1(Reg1_Out), .in2(Reg2_Out), .in3(Reg3_Out), .in4(Reg4_Out), .in5(Reg5_Out),
    .in6(Reg6_Out), .in7(Reg7_Out), .in8(Reg8_Out), .in9(Reg9_Out), .in10(Reg10_Out), .in11(Reg11_Out),
    .in12(Reg12_Out), .in13(Reg13_Out), .in14(Reg14_Out), .in15(Reg15_Out), .out(A_Out), .sel(A_Sel_In));
  Multiplexer #(.enable("false"), .select(4), .width(4)) multiplexer_2 (
    .in0(Reg0_Out), .in1(Reg1_Out), .in2(Reg2_Out), .in3(Reg3_Out), .in4(Reg4_Out), .in5(Reg5_Out),
    .in6(Reg6_Out), .in7(Reg7_Out), .in8(Reg8_Out), .in9(Reg9_Out), .in10(Reg10_Out), .in11(Reg11_Out),
    .in12(Reg12_Out), .in13(Reg13_Out), .in14(Reg14_Out), .in15(Reg15_Out), .out(B_Out), .sel(B_Sel_In));

  // Other names for the same wires on the sheet: A[3:0] = A_Out; A_Sel[3:0] = A_Sel_In; B[3:0] = B_Out;
  //   B_Sel[3:0] = B_Sel_In; C_Sel[3:0] = C_Sel_In; clk = clk_in; Data[3:0] = Data_In; Reg0[3:0] = Reg0_Out;
  //   Reg1[3:0] = Reg1_Out; Reg2[3:0] = Reg2_Out; Reg3[3:0] = Reg3_Out; Reg4[3:0] = Reg4_Out; Reg5[3:0] = Reg5_Out;
  //   Reg6[3:0] = Reg6_Out; Reg7[3:0] = Reg7_Out; Reg8[3:0] = Reg8_Out; Reg9[3:0] = Reg9_Out; Reg10[3:0] = Reg10_Out;
  //   Reg11[3:0] = Reg11_Out; Reg12[3:0] = Reg12_Out; Reg13[3:0] = Reg13_Out; Reg14[3:0] = Reg14_Out;
  //   Reg15[3:0] = Reg15_Out; Reg_Write = Reg_Write_In
endmodule

module ALU (
  input  [3:0] ALU_OPin,
  input  [3:0] Ain,
  input  [3:0] Bin,
  output [3:0] ALUresult
);

  wire [3:0] adder_1_out, adder_2_out, and_1_out, and_2_out, negator_1_out, not_1_out, or_1_out, or_2_out,
       subtractor_1_out, subtractor_2_out, xor_1_out, xor_2_out;

  assign not_1_out = ~Ain;  // NOT_Gate not_1, 4 bits wide
  Negator #(.width(4)) negator_1 (.in(Ain), .out(negator_1_out));
  Adder #(.width(4)) adder_1 (.a(Ain), .b(Bin), .out(adder_1_out));  // open: cin, cout
  Adder #(.width(4)) adder_2 (.a(Ain), .b(Bin), .out(adder_2_out));  // open: cin, cout
  Subtractor #(.width(4)) subtractor_1 (.a(Ain), .b(Bin), .out(subtractor_1_out));  // open: bin, bout
  Subtractor #(.width(4)) subtractor_2 (.a(Ain), .b(Bin), .out(subtractor_2_out));  // open: bin, bout
  assign xor_1_out = Ain ^ Bin;  // XOR_Gate xor_1, 4 bits wide
  assign xor_2_out = Ain ^ Bin;  // XOR_Gate xor_2, 4 bits wide
  assign or_1_out = Ain | Bin;  // OR_Gate or_1, 4 bits wide
  assign or_2_out = Ain | Bin;  // OR_Gate or_2, 4 bits wide
  assign and_1_out = Ain & Bin;  // AND_Gate and_1, 4 bits wide
  assign and_2_out = Ain & Bin;  // AND_Gate and_2, 4 bits wide
  Multiplexer #(.enable("false"), .select(4), .width(4)) multiplexer_1 (
    .in0(4'b0000), .in1(4'b0000), .in2(Bin), .in3(Ain), .in4(and_2_out), .in5(and_1_out), .in6(or_2_out),
    .in7(or_1_out), .in8(xor_1_out), .in9(xor_2_out), .in10(not_1_out), .in11(negator_1_out),
    .in12(adder_1_out), .in13(adder_2_out), .in14(subtractor_1_out), .in15(subtractor_2_out),
    .out(ALUresult), .sel(ALU_OPin));

  // Other names for the same wires on the sheet: A[3:0] = Ain; B[3:0] = Bin; Immediate[3:0] = Bin
endmodule

module InstructionDecoder (
  input  [3:0] OpCodeIn,
  output RegWrite,
  output isImmediate,
  output isStop
);

  wire and_1_out, and_2_out, and_3_out, not_1_out, not_2_out, not_3_out, not_4_out;

  not not_1 (not_1_out, OpCodeIn[3]);
  not not_2 (not_2_out, OpCodeIn[2]);
  not not_3 (not_3_out, OpCodeIn[1]);
  not not_4 (not_4_out, OpCodeIn[0]);
  or or_1 (RegWrite, OpCodeIn[1], OpCodeIn[2], OpCodeIn[3]);
  and and_1 (and_1_out, not_1_out, not_2_out, OpCodeIn[1], not_4_out);
  and and_2 (and_2_out, OpCodeIn[2], OpCodeIn[0]);
  and and_3 (and_3_out, OpCodeIn[3], not_3_out, OpCodeIn[0]);
  and and_4 (isStop, not_1_out, not_2_out, not_3_out, not_4_out);
  or or_2 (isImmediate, and_1_out, and_2_out, and_3_out);
endmodule
